# Fritzing sketch OliveTurtle (saved by Fritzing 0.9.4)
circuit board: 8.46667cm x 5.64444cm
breadboards: 2

parts:
  MH-ET_LIVE_ESP32_DEVKIT1 = MH-ET LIVE ESP32 DEVKIT 38 pins
  L-IN_12V = Camdenboss CTB0158-2 [part_number=CTB0158-2 package=THT]
  L1-T = Basic FET N-Channel [part_number=IRF520 package="TO220 [THT]"]
  L1 = Camdenboss CTB0158-2 [part_number=CTB0158-2 package=THT]
  L1-PC = TLP621 [package=THT]
  L1-R1 = Resistor [tolerance=±5% resistance=330 package="0603 [SMD]"]
  L1-R2 = Resistor [tolerance=±5% resistance=2.2k package="0603 [SMD]"]
  L2 = Camdenboss CTB0158-2 [part_number=CTB0158-2 package=THT]
  L2-T = Basic FET N-Channel [part_number=IRF520 package="TO220 [THT]"]
  L2-PC = TLP621 [package=THT]
  L2-R1 = Resistor [tolerance=±5% resistance=330 package="0603 [SMD]"]
  L2-R2 = Resistor [tolerance=±5% resistance=2.2k package="0603 [SMD]"]

nets:
  N1: MH-ET_LIVE_ESP32_DEVKIT1.GND#70, L1-PC.Pin_2, L2-PC.Pin_2
  N2: MH-ET_LIVE_ESP32_DEVKIT1.IO17, L1-R1.Pin_0
  N3: MH-ET_LIVE_ESP32_DEVKIT1.IO16, L2-R1.Pin_0
  N4: L-IN_12V.pin1, L1.pin1, L1-PC.Pin_3, L2.pin1, L2-PC.Pin_3
  N5: L-IN_12V.pin2, L1-T.drain, L2-T.drain
  12V: L-IN_12V.terminal_1
  GND: L-IN_12V.terminal_2
  N6: L1-T.gate, L1-R2.Pin_1
  N7: L1-T.source, L1.pin2
  N8: L1-PC.Pin_1, L1-R1.Pin_1
  N9: L1-PC.Pin_4, L1-R2.Pin_0
  N10: L2.pin2, L2-T.source
  N11: L2-T.gate, L2-R2.Pin_1
  N12: L2-PC.Pin_1, L2-R1.Pin_1
  N13: L2-PC.Pin_4, L2-R2.Pin_0

custom parts:
  MH-ET LIVE ESP32 DEVKIT 38 pins: http://mh.nodebb.com/topic/2/mh-et-live-esp32-devkit
